# Fritzing sketch samid (saved by Fritzing 0.9.3b)
breadboards: 1

parts:
  Componente1 = Arduino Uno (Rev3)
  LCD1 = LCD screen [part_number=hbh]
  S1 = Pushbutton [package="[THT]"]  # not connected
  S2 = Pushbutton [package="[THT]"]  # not connected
  S3 = Pushbutton [package="[THT]"]  # not connected
  S4 = Pushbutton [package="[THT]"]  # not connected
  S5 = Pushbutton [package="[THT]"]
  S6 = Pushbutton [package="[THT]"]
  R1 = Resistor [tolerance=±5% resistance=220 package=THT]
  R2 = Resistor [tolerance=±5% resistance=220 package=THT]  # not connected
  R3 = Resistor [tolerance=±5% resistance=220 package=THT]
  R4 = Resistor [tolerance=±5% resistance=220 package=THT]
  R5 = Resistor [tolerance=±5% resistance=220 package=THT]
  R6 = Resistor [tolerance=±5% resistance=220 package=THT]
  R7 = Resistor [tolerance=±5% resistance=220 package=THT]
  LED1 = LED - 5mm [color="Red (633nm)" package="5 mm [THT]"]
  R8 = Resistor [tolerance=±5% resistance=220 package=THT]
  R9 = Photocell (LDR) [package=THT]
  R10 = Resistor [tolerance=±5% resistance=220 package=THT]
  Componente2 = Soil Moisture Sensor
  U1 = RELAY [package=relay-jzc]
  VALVE2 = Plastic_Solenoid_Valve
  Water_Level_Sensor2 = richardbruneau00000

nets:
  N1: Componente1.A1, Componente2.SIG
  N2: Componente1.A3, Water_Level_Sensor2.connector8
  N3: Componente1.A5/SCL, R9.pin_0, R10.Pin_1
  N4: Componente1.D9_PWM, U1.COIL2
  N5: Componente1.D11_PWM/MOSI, LCD1.E
  N6: Componente1.D12/MISO, LCD1.RS
  N7: Componente1.D2, LCD1.DB7
  N8: Componente1.D3_PWM, LCD1.DB6
  N9: Componente1.D4, LCD1.DB5
  N10: Componente1.D5_PWM, LCD1.DB4
  N11: Componente1.D7, LCD1.LED+
  GND: Componente1.GND, LCD1.VSS, LCD1.V0
  VDD: LCD1.VDD, R7.Pin_1, R9.pin_1, Componente2.VCC, U1.NO, Water_Level_Sensor2.connector9
  N12: LCD1.R/W, LCD1.LED-
  N13: S5.Pin_1, S5.Pin_3, R1.Pin_0
  N14: S6.Pin_1, S6.Pin_2
  N15: R3.Pin_0, R6.Pin_1
  N16: R4.Pin_0, R6.Pin_0
  N17: R5.Pin_0, R7.Pin_0
  N18: LED1.cathode, R8.Pin_1
  N19: LED1.anode, Componente2.GND, U1.NC
  N20: U1.MAIN, VALVE2.connector2
